# Fritzing sketch cats (saved by Fritzing 0.7.11b)
breadboards: 1

parts:
  Arduino1 = Arduino
  J1 = Basic Servo
  J2 = Basic Servo
  J3 = Basic Servo
  J4 = Basic Servo
  JACK1 = 2.1mm Barrel Jack with Terminal Block
  JACK2 = 2.1mm Barrel Jack with Terminal Block
  J5 = Screw terminal - 2 pins [package=THT]
  J6 = Screw terminal - 2 pins [package=THT]
  J7 = Screw terminal - 2 pins [package=THT]
  J8 = Screw terminal - 2 pins [package=THT]
  K1 = Relay [part_number=FRS1B-S package=THT]
  J9 = Screw terminal - 2 pins [package=THT]
  Q1 = NPN-Transistor [package="TO92 [THT]"]
  R1 = 10k Ω Resistor [package=THT]
  D1 = Rectifier Diode [part_number=1N4001 package="300 mil [THT]"]

nets:
  GND: Arduino1.GND, J1.gnd, J2.gnd, J3.gnd, J4.gnd, JACK1.NEG, JACK2.NEG, J5.pin2, J7.pin2, Q1.C
  N1: Arduino1.D12, J8.pin1
  N2: Arduino1.D11, J4.pulse
  N3: Arduino1.D10, J3.pulse
  N4: Arduino1.D9, J2.pulse
  N5: Arduino1.D8, J1.pulse
  N6: Arduino1.D3, R1.Pin_0
  N7: Arduino1.D2, J6.pin1, J6.pin2
  N8: Arduino1.+5V, K1.C1, K1.C2, Q1.E, D1.cathode, D1.anode
  N9: Arduino1.VIN, JACK2.POS, J5.pin1
  VCC: J3.vcc, J4.vcc, JACK1.POS, J7.pin1
  N10: K1.COIL2, J9.pin2
  N11: K1.B, J9.pin1
  N12: Q1.B, R1.Pin_1

notes:
  5V Power Supply
  12V Power Supply
  Adafruit Coin selector
  12V
  GND
  PULSE
  Pololu LED strip
  5V
  GND
  DATA
  GATO 1
  GATO 2
  GATO 3
  GATO 4
  Relay for the wine pump
  Wine Pump
  220V in
  220V out
